# Fritzing sketch prototype schematic (saved by Fritzing 1.0.2b)
breadboards: 2

parts:
  RHT1 = Humidity and Temperature Sensor RHT03
  M1 = RioRand LM2596
  F1 = Fan - 4 wire [package=THT]
  Part2 = Adafruit ESP32 Feather V2
  Mod1 = MQ-7 breakout
  F2 = Fan - 4 wire [package=THT]
  S2 = Pushbutton [package="[SMD]"]
  S3 = Pushbutton [package="[SMD]"]
  S4 = Pushbutton [package="[SMD]"]
  S5 = Pushbutton [package="[SMD]"]
  Grove1 = Grove OLED 128x96
  JACK1 = 2.1mm Barrel Jack with Terminal Block
  M2 = 1 chan 5v relay module

nets:
  VCC: RHT1.Vcc, Part2.3.3V, Mod1.VCC, S2.Pin_3, S2.Pin_4, S3.Pin_3, S3.Pin_4, S4.Pin_3, S4.Pin_4, S5.Pin_3, S5.Pin_4, Grove1.VCC
  N1: RHT1.Data-signal, Part2.SDA, Part2.IO27_A10, Grove1.SDA
  GND: RHT1.GND_2, M1.Pin_2, M1.Pin_4, F1.GND, Part2.A3_I39, Part2.A2_I34, Part2.A1_DAC1, Part2.A0_DAC2, Part2.GND, Mod1.GND, F2.GND, S2.Pin_1, S2.Pin_2, S3.Pin_1, S3.Pin_2, S4.Pin_1, S4.Pin_2, S5.Pin_1, S5.Pin_2, Grove1.GND, JACK1.NEG
  N2: M1.Pin_1, JACK1.POS, M2.pin_2, M2.pin_5
  N3: M1.Pin_3, Part2.VBUS, M2.pin_1
  N4: F1.Power, F2.Power, M2.pin_4
  N5: F1.PWM, F1.Tach, Part2.IO12_A11
  N6: Part2.SCL, Grove1.SCL
  N7: Part2.IO13_A12, Mod1.AO
  N8: Part2.IO32_A7, M2.pin_3
  N9: Part2.IO14_A6, F2.Tach

notes:
  12 V

custom parts:
  Fan - 4 wire: Fan, 4 wire with tach.
  MQ-7 breakout: MQ-5 gas sensor
  1 chan 5v relay module: 1 Channel 5V Relay Module Board Shield with Optocoupler Support High and Low Level Trigger for Arduino.
